# Fritzing sketch BCM (saved by Fritzing 0.9.5d)
circuit board: 10.5cm x 8.5cm
breadboards: 1

parts:
  LED1 = LED - 5mm [color="Red (633nm)" package="5 mm [THT]"]
  Mpu = InvenSense MPU6050
  R1 = Resistor [tolerance=±5% resistance=220 package=THT]
  SD_READER = MicroSD Card Module
  Pressure = Adafruit BMP280 [part_number="Adafruit #2651"]
  Gas = Adafruit SGP30 Gas Sensor
  Temp = DHT22 Humidity and Temperature Sensor
  UNO = Arduino Uno (Rev3)

nets:
  N1: LED1.anode, R1.Pin_0
  VCC: Mpu.VCC, SD_READER.VCC, Pressure.VCC, Gas.VIN, Temp.VDD
  GND: Mpu.GND, SD_READER.GND, Pressure.GND, Gas.GND, Temp.GND, UNO.GND
  N2: Mpu.SCL, Pressure.SCK/SCL, Gas.SCL, UNO.A5/SCL
  N3: Mpu.SDA, Pressure.SDI/SDA, Gas.SDA, UNO.A4/SDA
  N4: Mpu.INT, UNO.D2
  N5: R1.Pin_1, UNO.D5_PWM
  N6: SD_READER.MISO, UNO.D12/MISO
  N7: SD_READER.MOSI, UNO.D11_PWM/MOSI
  N8: SD_READER.SCK, UNO.D13/SCK
  N9: SD_READER.CS, UNO.D10_PWM/SS
  N10: Temp.DATA, UNO.D3_PWM

notes:
  scl/sda

custom parts:
  Adafruit BMP280: Bosch has stepped up their game with their new BMP280 sensor, an environmental sensor with temperature, barometric pressure that is the next generation upgrade to the BMP085/BMP180/BMP183. This sensor is great for all sorts of weather sensing and can even be used in both I2C and SPI! This precision sensor from Bosch is the best low-cost, precision sensing solution for measuring barometric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
